// Logisim project 8bit.circ as structural Verilog: 15 circuits, main circuit clock_timer
module main (
  input  SELECT_SWITCH,
  input  MANUAL,
  input  HALT,
  input  RESET_program_counter,
  output USE_ALU_ADD_A_AND_B_REGISTERS
);

  wire add_out, and_1_out, and_2_out, and_3_out, and_4_out, and_5_out, clock_timer_1_out_5, decoder_1_out0,
       decoder_1_out1, decoder_1_out2, decoder_1_out3, decoder_1_out4, decoder_1_out5, decoder_1_out6,
       decoder_1_out7, decoder_1_out8, decoder_1_out9, decoder_1_out10, decoder_1_out11, decoder_1_out12,
       decoder_1_out13, decoder_1_out14, decoder_1_out15, load_out, not_1_out, not_2_out, not_3_out,
       not_4_out, not_5_out, not_6_out, not_7_out, not_8_out, not_9_out, not_10_out, not_11_out, not_12_out,
       not_13_out, not_14_out, or_1_out, or_2_out, or_3_out, or_4_out, r1_out, r2_out, store_out,
       store_r1_out, store_r2_out, THE_CLOCK_out;
  wire [3:0] t_counter_4bit_1_t1;
  wire [7:0] A_register_q, B_register_q, MAR_q, pc_1_program_counter_8bit, RAM_instructions_dout;
  wire [15:0] IR_q, rom_1_data;

  Register MAR (.D(IR_q[7:0]), .en(or_4_out), .clk(clock_timer_1_out_5), .Q(MAR_q));  // open: clr
  Clock THE_CLOCK (.out(THE_CLOCK_out));
  and and_1 (and_1_out, decoder_1_out2, store_out);
  or or_1 (or_1_out, and_4_out, and_5_out);
  clock_timer clock_timer_1 (
    .clk(THE_CLOCK_out), .s(SELECT_SWITCH), .button(MANUAL), .hlt(HALT), .out_5(clock_timer_1_out_5));
  RAM RAM_instructions (
    .addr(MAR_q), .we(and_1_out), .oe(or_1_out), .clk(clock_timer_1_out_5), .din(RAM_instructions_dout),
    .dout(RAM_instructions_dout));
  pc pc_1 (
    .clk(clock_timer_1_out_5), .pc_enable(decoder_1_out2), .reset_pc(RESET_program_counter),
    .program_counter_8bit(pc_1_program_counter_8bit));
  or or_2 (or_2_out, and_4_out, and_2_out);
  or or_3 (or_3_out, and_5_out, and_3_out);
  Register A_register (
    .D(RAM_instructions_dout), .en(or_2_out), .clk(clock_timer_1_out_5), .Q(A_register_q));  // open: clr
  assign RAM_instructions_dout = store_r1_out ? A_register_q : 8'bz;  // Controlled_Buffer controlled_buffer_1
  assign RAM_instructions_dout = load_out ? IR_q[7:0] : 8'bz;  // Controlled_Buffer controlled_buffer_2
  ROM #(.dataWidth(16)) rom_1 (.addr(pc_1_program_counter_8bit), .data(rom_1_data));
  Register B_register (
    .D(RAM_instructions_dout), .en(or_3_out), .clk(clock_timer_1_out_5), .Q(B_register_q));  // open: clr
  assign RAM_instructions_dout = store_r2_out ? B_register_q : 8'bz;  // Controlled_Buffer controlled_buffer_3
  Register #(.width(16)) IR (.D(rom_1_data), .en(decoder_1_out0), .clk(clock_timer_1_out_5), .Q(IR_q));  // open: clr
  t_counter_4bit t_counter_4bit_1 (
    .clk(clock_timer_1_out_5), .reset_pc(decoder_1_out3), .t1(t_counter_4bit_1_t1[0]),
    .t2(t_counter_4bit_1_t1[1]), .t3(t_counter_4bit_1_t1[2]), .t4(t_counter_4bit_1_t1[3]));
  Decoder #(.enable("false"), .select(4)) decoder_1 (
    .out0(decoder_1_out0), .out1(decoder_1_out1), .out2(decoder_1_out2), .out3(decoder_1_out3),
    .out4(decoder_1_out4), .out5(decoder_1_out5), .out6(decoder_1_out6), .out7(decoder_1_out7),
    .out8(decoder_1_out8), .out9(decoder_1_out9), .out10(decoder_1_out10), .out11(decoder_1_out11),
    .out12(decoder_1_out12), .out13(decoder_1_out13), .out14(decoder_1_out14), .out15(decoder_1_out15),
    .sel(t_counter_4bit_1_t1));
  not not_1 (not_1_out, IR_q[13]);
  not not_2 (not_2_out, IR_q[14]);
  not not_3 (not_3_out, IR_q[15]);
  not not_4 (not_4_out, IR_q[12]);
  not not_5 (not_5_out, IR_q[14]);
  not not_6 (not_6_out, IR_q[15]);
  not not_7 (not_7_out, IR_q[14]);
  not not_8 (not_8_out, IR_q[15]);
  not not_9 (not_9_out, IR_q[9]);
  not not_10 (not_10_out, IR_q[10]);
  not not_11 (not_11_out, IR_q[11]);
  not not_12 (not_12_out, IR_q[8]);
  not not_13 (not_13_out, IR_q[10]);
  not not_14 (not_14_out, IR_q[11]);
  and load (load_out, IR_q[12], not_1_out, not_2_out, not_3_out);
  and store (store_out, not_4_out, IR_q[13], not_5_out, not_6_out);
  and add (add_out, IR_q[12], IR_q[13], not_7_out, not_8_out);
  and ADD_REG (USE_ALU_ADD_A_AND_B_REGISTERS, IR_q[12], IR_q[13], IR_q[14], IR_q[15]);
  and r1 (r1_out, IR_q[8], not_9_out, not_10_out, not_11_out);
  and r2 (r2_out, not_12_out, IR_q[9], not_13_out, not_14_out);
  or or_4 (or_4_out, store_out, add_out);
  and and_2 (and_2_out, r1_out, load_out);
  and and_3 (and_3_out, r2_out, load_out);
  and store_r1 (store_r1_out, r1_out, store_out);
  and store_r2 (store_r2_out, r2_out, store_out);
  and and_4 (and_4_out, r1_out, add_out);
  and and_5 (and_5_out, r2_out, add_out);

  // Notes on the sheet:
  //   contents of rom_1 (hex, n*v repeats v):
  //   1150 1264 2100 2201 1114 123c 2102 2203 2104 2205 2106 2207 3100 3201
endmodule

module clock_timer (
  input  clk,
  input  s,
  input  button,
  input  hlt,
  output out_5
);

  wire and_1_out, and_2_out, not_1_out, not_2_out, or_1_out;

  not not_1 (not_1_out, hlt);
  not not_2 (not_2_out, s);
  and and_1 (and_1_out, clk, s);
  and and_2 (and_2_out, not_2_out, button);
  or or_1 (or_1_out, and_1_out, and_2_out);
  and and_3 (out_5, or_1_out, not_1_out);
endmodule

module sr_latch (
  input  R,
  input  S,
  output Q,
  output Qnot
);

  nor nor_1 (Q, R, Qnot);
  nor nor_2 (Qnot, Q, S);
endmodule

module d_latch (
  input  enable,
  input  d,
  output Q,
  output Qnot
);

  wire and_1_out, and_2_out, not_1_out;

  not not_1 (not_1_out, d);
  and and_1 (and_1_out, not_1_out, enable);
  and and_2 (and_2_out, enable, d);
  sr_latch sr_latch_1 (.R(and_1_out), .S(and_2_out), .Q(Q), .Qnot(Qnot));
endmodule

module d_flipflop (
  input  clk,
  input  d,
  output Q,
  output Qnot
);

  wire d_latch_1_q, not_1_out;

  not not_1 (not_1_out, clk);
  d_latch d_latch_1 (.enable(not_1_out), .d(d), .Q(d_latch_1_q));  // open: Qnot
  d_latch d_latch_2 (.enable(clk), .d(d_latch_1_q), .Q(Q), .Qnot(Qnot));
endmodule

module onebyteregister (
  input  enable,
  input  clk,
  input  load,
  input  d0,
  input  d1,
  input  d2,
  input  d3,
  input  d4,
  input  d5,
  input  d6,
  input  d7,
  output q0,
  output q1,
  output q2,
  output q3,
  output q4,
  output q5,
  output q6,
  output q7
);

  wire d_flipflop_1_q, d_flipflop_2_q, d_flipflop_3_q, d_flipflop_4_q, d_flipflop_5_q, d_flipflop_6_q,
       d_flipflop_7_q, d_flipflop_8_q, load_input_1_flipflopinput, load_input_2_flipflopinput,
       load_input_3_flipflopinput, load_input_4_flipflopinput, load_input_5_flipflopinput,
       load_input_6_flipflopinput, load_input_7_flipflopinput, load_input_8_flipflopinput;

  load_input load_input_1 (.qn(d_flipflop_1_q), .load(load), .dn(d0), .flipflopinput(load_input_1_flipflopinput));
  load_input load_input_2 (.qn(d_flipflop_2_q), .load(load), .dn(d1), .flipflopinput(load_input_2_flipflopinput));
  load_input load_input_3 (.qn(d_flipflop_3_q), .load(load), .dn(d2), .flipflopinput(load_input_3_flipflopinput));
  load_input load_input_4 (.qn(d_flipflop_4_q), .load(load), .dn(d3), .flipflopinput(load_input_4_flipflopinput));
  load_input load_input_5 (.qn(d_flipflop_5_q), .load(load), .dn(d4), .flipflopinput(load_input_5_flipflopinput));
  load_input load_input_6 (.qn(d_flipflop_6_q), .load(load), .dn(d5), .flipflopinput(load_input_6_flipflopinput));
  load_input load_input_7 (.qn(d_flipflop_7_q), .load(load), .dn(d6), .flipflopinput(load_input_7_flipflopinput));
  load_input load_input_8 (.qn(d_flipflop_8_q), .load(load), .dn(d7), .flipflopinput(load_input_8_flipflopinput));
  d_flipflop d_flipflop_1 (.clk(clk), .d(load_input_1_flipflopinput), .Q(d_flipflop_1_q));  // open: Qnot
  d_flipflop d_flipflop_2 (.clk(clk), .d(load_input_2_flipflopinput), .Q(d_flipflop_2_q));  // open: Qnot
  d_flipflop d_flipflop_3 (.clk(clk), .d(load_input_3_flipflopinput), .Q(d_flipflop_3_q));  // open: Qnot
  d_flipflop d_flipflop_4 (.clk(clk), .d(load_input_4_flipflopinput), .Q(d_flipflop_4_q));  // open: Qnot
  d_flipflop d_flipflop_5 (.clk(clk), .d(load_input_5_flipflopinput), .Q(d_flipflop_5_q));  // open: Qnot
  d_flipflop d_flipflop_6 (.clk(clk), .d(load_input_6_flipflopinput), .Q(d_flipflop_6_q));  // open: Qnot
  d_flipflop d_flipflop_7 (.clk(clk), .d(load_input_7_flipflopinput), .Q(d_flipflop_7_q));  // open: Qnot
  d_flipflop d_flipflop_8 (.clk(clk), .d(load_input_8_flipflopinput), .Q(d_flipflop_8_q));  // open: Qnot
  assign q1 = enable ? d_flipflop_2_q : 1'bz;  // Controlled_Buffer controlled_buffer_1
  assign q3 = enable ? d_flipflop_4_q : 1'bz;  // Controlled_Buffer controlled_buffer_2
  assign q4 = enable ? d_flipflop_5_q : 1'bz;  // Controlled_Buffer controlled_buffer_3
  assign q5 = enable ? d_flipflop_6_q : 1'bz;  // Controlled_Buffer controlled_buffer_4
  assign q6 = enable ? d_flipflop_7_q : 1'bz;  // Controlled_Buffer controlled_buffer_5
  assign q7 = enable ? d_flipflop_8_q : 1'bz;  // Controlled_Buffer controlled_buffer_6
  assign q0 = enable ? d_flipflop_1_q : 1'bz;  // Controlled_Buffer controlled_buffer_7
  assign q2 = enable ? d_flipflop_3_q : 1'bz;  // Controlled_Buffer controlled_buffer_8
endmodule

module load_input (
  input  qn,
  input  load,
  input  dn,
  output flipflopinput
);

  wire and_1_out, and_2_out, not_1_out;

  not not_1 (not_1_out, load);
  and and_1 (and_1_out, load, dn);
  and and_2 (and_2_out, qn, not_1_out);
  or or_1 (flipflopinput, and_2_out, and_1_out);
endmodule

module addition (
  input  a0,
  input  b0,
  input  a1,
  input  b1,
  input  a2,
  input  b2,
  input  a3,
  input  b3,
  input  a4,
  input  b4,
  input  a5,
  input  b5,
  input  a6,
  input  b6,
  input  a7,
  input  b7,
  output c0,
  output c1,
  output c2,
  output c3,
  output c4,
  output c5,
  output c6,
  output c7,
  output carry
);

  wire and_1_out, carry_in_add_1_c_out, carry_in_add_2_c_out, carry_in_add_3_c_out, carry_in_add_4_c_out,
       carry_in_add_5_c_out, carry_in_add_6_c_out;

  and and_1 (and_1_out, a0, b0);
  xor xor_1 (c0, a0, b0);
  carry_in_add carry_in_add_1 (.c_in(and_1_out), .bit_a(a1), .bit_b(b1), .added(c1), .c_out(carry_in_add_1_c_out));
  carry_in_add carry_in_add_2 (
    .c_in(carry_in_add_1_c_out), .bit_a(a2), .bit_b(b2), .added(c2), .c_out(carry_in_add_2_c_out));
  carry_in_add carry_in_add_3 (
    .c_in(carry_in_add_2_c_out), .bit_a(a3), .bit_b(b3), .added(c3), .c_out(carry_in_add_3_c_out));
  carry_in_add carry_in_add_4 (
    .c_in(carry_in_add_3_c_out), .bit_a(a4), .bit_b(b4), .added(c4), .c_out(carry_in_add_4_c_out));
  carry_in_add carry_in_add_5 (
    .c_in(carry_in_add_4_c_out), .bit_a(a5), .bit_b(b5), .added(c5), .c_out(carry_in_add_5_c_out));
  carry_in_add carry_in_add_6 (
    .c_in(carry_in_add_5_c_out), .bit_a(a6), .bit_b(b6), .added(c6), .c_out(carry_in_add_6_c_out));
  carry_in_add carry_in_add_7 (.c_in(carry_in_add_6_c_out), .bit_a(a7), .bit_b(b7), .added(c7), .c_out(carry));
endmodule

module carry_in_add (
  input  c_in,
  input  bit_a,
  input  bit_b,
  output added,
  output c_out
);

  wire and_1_out, and_2_out, xor_1_out;

  xor xor_1 (xor_1_out, bit_a, bit_b);
  and and_1 (and_1_out, bit_a, bit_b);
  xor xor_2 (added, c_in, xor_1_out);
  and and_2 (and_2_out, c_in, xor_1_out);
  or or_1 (c_out, and_2_out, and_1_out);
endmodule

module onebyte (
  input  output_enable,
  input  clk,
  input  load_enable,
  input  [7:0] input_8bit,
  output [7:0] output_8bit
);

  wire [7:0] onebyteregister_1_q0;

  onebyteregister onebyteregister_1 (
    .enable(output_enable), .clk(clk), .load(load_enable), .d0(input_8bit[0]), .d1(input_8bit[1]),
    .d2(input_8bit[2]), .d3(input_8bit[3]), .d4(input_8bit[4]), .d5(input_8bit[5]), .d6(input_8bit[6]),
    .d7(input_8bit[7]), .q0(onebyteregister_1_q0[0]), .q1(onebyteregister_1_q0[1]),
    .q2(onebyteregister_1_q0[2]), .q3(onebyteregister_1_q0[3]), .q4(onebyteregister_1_q0[4]),
    .q5(onebyteregister_1_q0[5]), .q6(onebyteregister_1_q0[6]), .q7(onebyteregister_1_q0[7]));
  assign output_8bit = load_enable ? onebyteregister_1_q0 : 8'bz;  // Controlled_Buffer controlled_buffer_1
endmodule

module thirytwobyte (
  input  clk,
  input  output_enable,
  input  in_3,
  input  in_4,
  input  in_5,
  input  in_6,
  input  in_7,
  input  in_8,
  input  in_9,
  input  in_10,
  input  in_11,
  input  in_12,
  input  in_13,
  input  in_14,
  input  in_15,
  input  in_16,
  input  in_17,
  input  in_18,
  input  in_19,
  input  in_20,
  input  in_21,
  input  in_22,
  input  in_23,
  input  in_24,
  input  in_25,
  input  in_26,
  input  in_27,
  input  in_28,
  input  in_29,
  input  in_30,
  input  in_31,
  input  in_32,
  input  in_33,
  input  in_34,
  input  [7:0] in_35,
  output [7:0] memory_output
);

  onebyte onebyte_1 (
    .output_enable(output_enable), .clk(clk), .load_enable(in_3), .input_8bit(in_35),
    .output_8bit(memory_output));
  onebyte onebyte_2 (
    .output_enable(output_enable), .clk(clk), .load_enable(in_10), .input_8bit(in_35),
    .output_8bit(memory_output));
  onebyte onebyte_3 (
    .output_enable(output_enable), .clk(clk), .load_enable(in_17), .input_8bit(in_35),
    .output_8bit(memory_output));
  onebyte onebyte_4 (
    .output_enable(output_enable), .clk(clk), .load_enable(in_23), .input_8bit(in_35),
    .output_8bit(memory_output));
  onebyte onebyte_5 (
    .output_enable(output_enable), .clk(clk), .load_enable(in_29), .input_8bit(in_35),
    .output_8bit(memory_output));
  onebyte onebyte_6 (
    .output_enable(output_enable), .clk(clk), .load_enable(in_4), .input_8bit(in_35),
    .output_8bit(memory_output));
  onebyte onebyte_7 (
    .output_enable(output_enable), .clk(clk), .load_enable(in_11), .input_8bit(in_35),
    .output_8bit(memory_output));
  onebyte onebyte_8 (
    .output_enable(output_enable), .clk(clk), .load_enable(in_18), .input_8bit(in_35),
    .output_8bit(memory_output));
  onebyte onebyte_9 (
    .output_enable(output_enable), .clk(clk), .load_enable(in_24), .input_8bit(in_35),
    .output_8bit(memory_output));
  onebyte onebyte_10 (
    .output_enable(output_enable), .clk(clk), .load_enable(in_30), .input_8bit(in_35),
    .output_8bit(memory_output));
  onebyte onebyte_11 (
    .output_enable(output_enable), .clk(clk), .load_enable(in_5), .input_8bit(in_35),
    .output_8bit(memory_output));
  onebyte onebyte_12 (
    .output_enable(output_enable), .clk(clk), .load_enable(in_12), .input_8bit(in_35),
    .output_8bit(memory_output));
  onebyte onebyte_13 (
    .output_enable(output_enable), .clk(clk), .load_enable(in_19), .input_8bit(in_35),
    .output_8bit(memory_output));
  onebyte onebyte_14 (
    .output_enable(output_enable), .clk(clk), .load_enable(in_25), .input_8bit(in_35),
    .output_8bit(memory_output));
  onebyte onebyte_15 (
    .output_enable(output_enable), .clk(clk), .load_enable(in_31), .input_8bit(in_35),
    .output_8bit(memory_output));
  onebyte onebyte_16 (
    .output_enable(output_enable), .clk(clk), .load_enable(in_6), .input_8bit(in_35),
    .output_8bit(memory_output));
  onebyte onebyte_17 (
    .output_enable(output_enable), .clk(clk), .load_enable(in_13), .input_8bit(in_35),
    .output_8bit(memory_output));
  onebyte onebyte_18 (
    .output_enable(output_enable), .clk(clk), .load_enable(in_20), .input_8bit(in_35),
    .output_8bit(memory_output));
  onebyte onebyte_19 (
    .output_enable(output_enable), .clk(clk), .load_enable(in_26), .input_8bit(in_35),
    .output_8bit(memory_output));
  onebyte onebyte_20 (
    .output_enable(output_enable), .clk(clk), .load_enable(in_32), .input_8bit(in_35),
    .output_8bit(memory_output));
  onebyte onebyte_21 (
    .output_enable(output_enable), .clk(clk), .load_enable(in_7), .input_8bit(in_35),
    .output_8bit(memory_output));
  onebyte onebyte_22 (
    .output_enable(output_enable), .clk(clk), .load_enable(in_14), .input_8bit(in_35),
    .output_8bit(memory_output));
  onebyte onebyte_23 (
    .output_enable(output_enable), .clk(clk), .load_enable(in_21), .input_8bit(in_35),
    .output_8bit(memory_output));
  onebyte onebyte_24 (
    .output_enable(output_enable), .clk(clk), .load_enable(in_27), .input_8bit(in_35),
    .output_8bit(memory_output));
  onebyte onebyte_25 (
    .output_enable(output_enable), .clk(clk), .load_enable(in_33), .input_8bit(in_35),
    .output_8bit(memory_output));
  onebyte onebyte_26 (
    .output_enable(output_enable), .clk(clk), .load_enable(in_8), .input_8bit(in_35),
    .output_8bit(memory_output));
  onebyte onebyte_27 (
    .output_enable(output_enable), .clk(clk), .load_enable(in_15), .input_8bit(in_35),
    .output_8bit(memory_output));
  onebyte onebyte_28 (
    .output_enable(output_enable), .clk(clk), .load_enable(in_22), .input_8bit(in_35),
    .output_8bit(memory_output));
  onebyte onebyte_29 (
    .clk(clk), .load_enable(in_28), .input_8bit(in_35), .output_8bit(memory_output));  // open: output_enable
  onebyte onebyte_30 (
    .output_enable(output_enable), .clk(clk), .load_enable(in_34), .input_8bit(in_35),
    .output_8bit(memory_output));
  onebyte onebyte_31 (
    .output_enable(output_enable), .clk(clk), .load_enable(in_9), .input_8bit(in_35),
    .output_8bit(memory_output));
  onebyte onebyte_32 (
    .output_enable(output_enable), .clk(clk), .load_enable(in_16), .input_8bit(in_35),
    .output_8bit(memory_output));
endmodule

module decoder_32bytes (
  input  clk,
  input  [7:0] input_8bit,
  input  output_enable,
  input  load_enable,
  input  [4:0] address,
  output [7:0] output_8bit
);

  wire decoder_1_out0, decoder_1_out1, decoder_1_out2, decoder_1_out3, decoder_1_out4, decoder_1_out5,
       decoder_1_out6, decoder_1_out7, decoder_1_out8, decoder_1_out9, decoder_1_out10, decoder_1_out11,
       decoder_1_out12, decoder_1_out13, decoder_1_out14, decoder_1_out15, decoder_1_out16, decoder_1_out17,
       decoder_1_out18, decoder_1_out19, decoder_1_out20, decoder_1_out21, decoder_1_out22, decoder_1_out23,
       decoder_1_out24, decoder_1_out25, decoder_1_out26, decoder_1_out27, decoder_1_out28, decoder_1_out29,
       decoder_1_out30, decoder_1_out31;

  Decoder #(.select(5)) decoder_1 (
    .out0(decoder_1_out0), .out1(decoder_1_out1), .out2(decoder_1_out2), .out3(decoder_1_out3),
    .out4(decoder_1_out4), .out5(decoder_1_out5), .out6(decoder_1_out6), .out7(decoder_1_out7),
    .out8(decoder_1_out8), .out9(decoder_1_out9), .out10(decoder_1_out10), .out11(decoder_1_out11),
    .out12(decoder_1_out12), .out13(decoder_1_out13), .out14(decoder_1_out14), .out15(decoder_1_out15),
    .out16(decoder_1_out16), .out17(decoder_1_out17), .out18(decoder_1_out18), .out19(decoder_1_out19),
    .out20(decoder_1_out20), .out21(decoder_1_out21), .out22(decoder_1_out22), .out23(decoder_1_out23),
    .out24(decoder_1_out24), .out25(decoder_1_out25), .out26(decoder_1_out26), .out27(decoder_1_out27),
    .out28(decoder_1_out28), .out29(decoder_1_out29), .out30(decoder_1_out30), .out31(decoder_1_out31),
    .sel(address), .en(load_enable));
  thirytwobyte thirytwobyte_1 (
    .in_6(decoder_1_out3), .in_13(decoder_1_out10), .in_20(decoder_1_out17), .in_26(decoder_1_out23),
    .in_32(decoder_1_out29), .in_7(decoder_1_out4), .in_14(decoder_1_out11), .in_21(decoder_1_out18),
    .in_27(decoder_1_out24), .in_33(decoder_1_out30), .in_8(decoder_1_out5), .in_15(decoder_1_out12),
    .in_22(decoder_1_out19), .in_28(decoder_1_out25), .in_34(decoder_1_out31), .output_enable(output_enable),
    .clk(clk), .in_9(decoder_1_out6), .in_16(decoder_1_out13), .in_35(input_8bit), .in_3(decoder_1_out0),
    .in_10(decoder_1_out7), .in_17(decoder_1_out14), .in_23(decoder_1_out20), .in_29(decoder_1_out26),
    .in_4(decoder_1_out1), .in_11(decoder_1_out8), .in_18(decoder_1_out15), .in_24(decoder_1_out21),
    .in_30(decoder_1_out27), .in_5(decoder_1_out2), .in_12(decoder_1_out9), .in_19(decoder_1_out16),
    .in_25(decoder_1_out22), .in_31(decoder_1_out28), .memory_output(output_8bit));
endmodule

module pc (
  input  clk,
  input  pc_enable,
  input  reset_pc,
  output [7:0] program_counter_8bit
);

  wire controlled_buffer_1_out, j_k_ff_1_qn, j_k_ff_2_qn, j_k_ff_3_qn, j_k_ff_4_qn, j_k_ff_5_qn, j_k_ff_6_qn,
       j_k_ff_7_qn, or_1_out;

  assign controlled_buffer_1_out = pc_enable ? clk : 1'bz;  // Controlled_Buffer controlled_buffer_1
  or or_1 (or_1_out, reset_pc, 1'b0);
  J_K_Flip_Flop j_k_ff_1 (
    .J(1'b1), .K(1'b1), .clk(controlled_buffer_1_out), .Q(program_counter_8bit[0]), .Qn(j_k_ff_1_qn),
    .reset(or_1_out));  // open: preset
  J_K_Flip_Flop j_k_ff_2 (
    .J(1'b1), .K(1'b1), .clk(j_k_ff_1_qn), .Q(program_counter_8bit[1]), .Qn(j_k_ff_2_qn), .reset(or_1_out));  // open: preset
  J_K_Flip_Flop j_k_ff_3 (
    .J(1'b1), .K(1'b1), .clk(j_k_ff_2_qn), .Q(program_counter_8bit[2]), .Qn(j_k_ff_3_qn), .reset(or_1_out));  // open: preset
  J_K_Flip_Flop j_k_ff_4 (
    .J(1'b1), .K(1'b1), .clk(j_k_ff_3_qn), .Q(program_counter_8bit[3]), .Qn(j_k_ff_4_qn), .reset(or_1_out));  // open: preset
  J_K_Flip_Flop j_k_ff_5 (
    .J(1'b1), .K(1'b1), .clk(j_k_ff_4_qn), .Q(program_counter_8bit[4]), .Qn(j_k_ff_5_qn), .reset(or_1_out));  // open: preset
  J_K_Flip_Flop j_k_ff_6 (
    .J(1'b1), .K(1'b1), .clk(j_k_ff_5_qn), .Q(program_counter_8bit[5]), .Qn(j_k_ff_6_qn), .reset(or_1_out));  // open: preset
  J_K_Flip_Flop j_k_ff_7 (
    .J(1'b1), .K(1'b1), .clk(j_k_ff_6_qn), .Q(program_counter_8bit[6]), .Qn(j_k_ff_7_qn), .reset(or_1_out));  // open: preset
  J_K_Flip_Flop j_k_ff_8 (
    .J(1'b1), .K(1'b1), .clk(j_k_ff_7_qn), .Q(program_counter_8bit[7]), .reset(or_1_out));  // open: Qn, preset
endmodule

module ALU (
  input  [7:0] A,
  input  [7:0] B,
  input  ALU_out_enable,
  output [7:0] added_value,
  output carry
);

  wire [7:0] addition_1_c0;

  addition addition_1 (
    .a0(A[0]), .b0(B[0]), .a1(A[1]), .b1(B[1]), .a2(A[2]), .b2(B[2]), .a3(A[3]), .b3(B[3]), .a4(A[4]),
    .b4(B[4]), .a5(A[5]), .b5(B[5]), .a6(A[6]), .b6(B[6]), .a7(A[7]), .b7(B[7]), .c0(addition_1_c0[0]),
    .c1(addition_1_c0[1]), .c2(addition_1_c0[2]), .c3(addition_1_c0[3]), .c4(addition_1_c0[4]),
    .c5(addition_1_c0[5]), .c6(addition_1_c0[6]), .c7(addition_1_c0[7]), .carry(carry));
  assign added_value = ALU_out_enable ? addition_1_c0 : 8'bz;  // Controlled_Buffer controlled_buffer_1
endmodule

module t_counter_4bit (
  input  clk,
  input  reset_pc,
  output t1,
  output t2,
  output t3,
  output t4
);

  wire j_k_ff_1_qn, j_k_ff_2_qn, j_k_ff_3_qn, or_1_out;

  or or_1 (or_1_out, reset_pc, 1'b0);
  J_K_Flip_Flop j_k_ff_1 (.J(1'b1), .K(1'b1), .clk(clk), .Q(t1), .Qn(j_k_ff_1_qn), .reset(or_1_out));  // open: preset
  J_K_Flip_Flop j_k_ff_2 (
    .J(1'b1), .K(1'b1), .clk(j_k_ff_1_qn), .Q(t2), .Qn(j_k_ff_2_qn), .reset(or_1_out));  // open: preset
  J_K_Flip_Flop j_k_ff_3 (
    .J(1'b1), .K(1'b1), .clk(j_k_ff_2_qn), .Q(t3), .Qn(j_k_ff_3_qn), .reset(or_1_out));  // open: preset
  J_K_Flip_Flop j_k_ff_4 (.J(1'b1), .K(1'b1), .clk(j_k_ff_3_qn), .Q(t4), .reset(or_1_out));  // open: Qn, preset
endmodule
